// Logisim project 3_Capteurs.circ as structural Verilog: 1 circuit, main circuit main
module main (
  input  E1,
  input  E2,
  input  E3,
  output out_4,
  output out_5
);

  wire and_1_out, and_2_out, not_1_out, not_2_out, not_3_out, not_4_out, not_5_out;

  not not_1 (not_1_out, E1);
  or or_1 (out_4, not_1_out, E2, E3);
  and and_1 (and_1_out, E1, not_3_out, not_2_out);
  not not_2 (not_2_out, E3);
  not not_3 (not_3_out, E2);
  or or_2 (out_5, and_1_out, and_2_out);
  not not_4 (not_4_out, E1);
  and and_2 (and_2_out, not_4_out, E2, not_5_out);
  not not_5 (not_5_out, E3);
endmodule
